# Fritzing sketch juke (saved by Fritzing 0.9.2b)
circuit board: 12.7cm x 20.3cm
breadboards: 2

parts:
  J1 = female pin header, 20 pins [form="♀ (female)"]
  Q1 = TRANSISTOR_NPN [package=to-92]
  Q2 = TRANSISTOR_NPN [package=to-92]
  Q3 = TRANSISTOR_NPN [package=to-92]
  Q4 = TRANSISTOR_NPN [package=to-92]
  R1 = Resistor [tolerance=±5% resistance=1k power=0pW package=THT]
  R2 = Resistor [tolerance=±5% resistance=1k power=0pW package=THT]
  R4 = Resistor [tolerance=±5% resistance=1k power=0pW package=THT]
  R8 = Resistor [tolerance=±5% resistance=1k power=0pW package=THT]
  R9 = Resistor [tolerance=±5% resistance=100k package=THT]
  R10 = Resistor [tolerance=±5% resistance=100k package=THT]
  R11 = Resistor [tolerance=±5% resistance=100k package=THT]
  R13 = Resistor [tolerance=±5% resistance=51k package=THT]
  R14 = Resistor [tolerance=±5% resistance=51k package=THT]
  R15 = Resistor [tolerance=±5% resistance=51k package=THT]
  Q5 = TRANSISTOR_NPN [package=to-92]
  Q6 = TRANSISTOR_NPN [package=to-92]
  Q7 = TRANSISTOR_NPN [package=to-92]
  Q8 = TRANSISTOR_NPN [package=to-92]
  R17 = Resistor [tolerance=±5% resistance=1k power=0pW package=THT]
  R19 = Resistor [tolerance=±5% resistance=1k power=0pW package=THT]
  R20 = Resistor [tolerance=±5% resistance=1k power=0pW package=THT]
  U1 = Voltage Regulator [package=to220-igo]
  J3 = male pin header, 4 pins [form="♂ (male)"]
  C1 = Electrolytic Capacitor [capacitance=10µF package="100 mil [THT, electrolytic]"]
  J2 = female pin header, 10 pins [form="♀ (female)"]
  J5 = female pin header, 9 pins [form="♀ (female)"]
  C2 = Electrolytic Capacitor [capacitance=10µF package="100 mil [THT, electrolytic]"]
  J7 = male pin header, 8 pins [form="♂ (male)"]
  J8 = male pin header, 12 pins [form="♂ (male)"]
  J9 = male pin header, 14 pins [form="♂ (male)"]
  J10 = male pin header, 10 pins [form="♂ (male)"]
  J11 = male pin header, 8 pins [form="♂ (male)"]
  U2 = RJ45 Jack [package=rj45-8]
  R3 = Resistor [tolerance=±20% resistance=10k package=THT]
  R5 = Resistor [tolerance=±20% resistance=10k package=THT]
  R7 = Resistor [tolerance=±20% resistance=10k package=THT]
  R21 = Resistor [tolerance=±5% resistance=1k power=0pW package=THT]
  R6 = Resistor [tolerance=±20% resistance=10k package=THT]
  J12 = male pin header, 1 pin [form="♂ (male)"]  # not connected
  J13 = male pin header, 1 pin [form="♂ (male)"]  # not connected
  J14 = male pin header, 1 pin [form="♂ (male)"]  # not connected
  J15 = male pin header, 1 pin [form="♂ (male)"]  # not connected
  J16 = male pin header, 1 pin [form="♂ (male)"]  # not connected
  J17 = male pin header, 1 pin [form="♂ (male)"]  # not connected
  J18 = male pin header, 1 pin [form="♂ (male)"]  # not connected
  J19 = male pin header, 1 pin [form="♂ (male)"]  # not connected
  J20 = male pin header, 1 pin [form="♂ (male)"]  # not connected
  J21 = male pin header, 1 pin [form="♂ (male)"]  # not connected
  J22 = male pin header, 1 pin [form="♂ (male)"]  # not connected
  J23 = male pin header, 1 pin [form="♂ (male)"]  # not connected
  J24 = male pin header, 1 pin [form="♂ (male)"]  # not connected

nets (from the breadboard view):
  N1: J1.pin2, J11.pin7
  N2: J1.pin3, J11.pin2
  N3: J1.pin4, J11.pin1
  N4: J1.pin5, J10.pin1
  N5: J1.pin6, J10.pin2
  N6: J1.pin8, J1.pin16, Q1.E, Q2.E, Q3.E, Q4.E, R13.Pin_0, R14.Pin_0, R15.Pin_0, Q5.E, Q6.E, Q7.E, Q8.E, U1.IN, J3.pin1, C1.+, J2.pin4, J2.pin6, J5.pin7, C2.+, J8.pin12, J9.pin1, J9.pin7, U2.5
  N7: J1.pin9, J10.pin3
  N8: J1.pin11, R19.Pin_0
  N9: J1.pin12, J1.pin20, J10.pin10, R3.Pin_0, R7.Pin_0
  N10: J1.pin14, R11.Pin_0, R15.Pin_1
  N11: J1.pin15, R10.Pin_0, R14.Pin_1
  N12: J1.pin17, R9.Pin_0, R13.Pin_1
  N13: J1.pin18, J9.pin9, J9.pin11
  N14: J1.pin19, J9.pin13, J9.pin14
  N15: Q1.B, R1.Pin_1
  N16: Q1.C, R2.Pin_1, R3.Pin_1
  N17: Q2.B, R2.Pin_0
  N18: Q2.C, U2.3, R5.Pin_0
  N19: Q3.B, R4.Pin_1
  N20: Q3.C, R8.Pin_1, R7.Pin_1
  N21: Q4.B, R8.Pin_0
  N22: Q4.C, U2.8, R6.Pin_0
  N23: R1.Pin_0, J5.pin1
  N24: R4.Pin_0, J2.pin10
  N25: R9.Pin_1, U2.4
  N26: R10.Pin_1, U2.7
  N27: R11.Pin_1, U2.6
  N28: Q5.B, R20.Pin_1
  N29: Q5.C, J7.pin8
  N30: Q6.B, R19.Pin_1
  N31: Q6.C, J7.pin5
  N32: Q7.B, R21.Pin_1
  N33: Q7.C, J7.pin4
  N34: Q8.B, R17.Pin_1
  N35: Q8.C, J7.pin3
  N36: R17.Pin_0, J5.pin6
  N37: R20.Pin_0, J5.pin4
  N38: U1.GND, C2.-, J8.pin10, R5.Pin_1, R6.Pin_1
  N39: U1.OUT, J3.pin4, C1.-
  N40: J2.pin1, J11.pin6
  N41: J2.pin2, J11.pin5
  N42: J2.pin3, J11.pin4
  N43: J2.pin5, J11.pin3
  N44: J5.pin2, J10.pin4
  N45: J5.pin5, R21.Pin_0
  N46: J5.pin9, J7.pin1, J9.pin3, J9.pin8
